# Fritzing sketch AntonioServoJoystick (saved by Fritzing 0.7.12b)
breadboards: 1

parts:
  Parte1 = Thumb Joystick
  Parte2 = Thumb Joystick
  Parte3 = Thumb Joystick
  Parte4 = Thumb Joystick
  J1 = Basic Servo
  J2 = Basic Servo
  J3 = Basic Servo
  J4 = Basic Servo
  U1 = Arduino Mega

nets:
  GND: Parte1.GND, Parte2.GND, Parte3.GND, Parte4.GND, J1.gnd, J2.gnd, J3.gnd, J4.gnd, U1.GND
  N1: Parte1.HORZ, U1.A11
  N2: Parte1.VERT, U1.A10
  VCC: Parte1.VCC, Parte2.VCC, Parte3.VCC, Parte4.VCC, J1.vcc, J2.vcc, J3.vcc, J4.vcc, U1.+5V
  N3: Parte2.HORZ, U1.A9
  N4: Parte2.VERT, U1.A8
  N5: Parte3.HORZ, U1.A3
  N6: Parte3.VERT, U1.A2
  N7: Parte4.HORZ, U1.A1
  N8: Parte4.VERT, U1.A0
  N9: J1.pulse, U1.D3
  N10: J2.pulse, U1.D2
  N11: J3.pulse, U1.D4
  N12: J4.pulse, U1.D5
