# Fritzing sketch LDR_Server_Arduino (saved by Fritzing 0.7.12b)
breadboards: 1

parts:
  Arduino_Ethernet_Shield1 = Arduino Ethernet Shield
  R1 = Photocell (LDR) [package=THT]
  R2 = 1k Ω Resistor [package=THT]

nets:
  N1: Arduino_Ethernet_Shield1.GND, R1.pin_1
  N2: Arduino_Ethernet_Shield1.+5V, R2.Pin_0
  N3: Arduino_Ethernet_Shield1.A2, R1.pin_0, R2.Pin_1
