# Fritzing sketch Arduino_EthernetShield_RGB_Scheme (saved by Fritzing 0.7.12b)
breadboards: 1

parts:
  Arduino_Ethernet_Shield = Arduino Ethernet Shield
  Arduino = Arduino
  R2 = Resistor [tolerance=±5% resistance=220 package="0805 [SMD]"]
  R3 = Resistor [tolerance=±5% resistance=220 package="0805 [SMD]"]
  R1 = Resistor [tolerance=±5% resistance=220 package="0805 [SMD]"]
  RGB_LED = RGB LED (com. cathode, rgb) [package="5 mm [THT]"]

nets (from the breadboard view):
  N1: Arduino_Ethernet_Shield.D6, R1.Pin_0
  N2: Arduino_Ethernet_Shield.D5, R2.Pin_1
  N3: Arduino_Ethernet_Shield.D3, R3.Pin_1
  N4: Arduino.GND, RGB_LED.common_cathode
  N5: R2.Pin_0, RGB_LED.green_anode
  N6: R3.Pin_0, RGB_LED.blue_anode
  N7: R1.Pin_1, RGB_LED.red_anode

notes:
  ARDUINO + ETHERNET SHIELD
  R1,R2,R3: 120 ohm
