# Fritzing sketch Notificación por PushingBox (saved by Fritzing 0.8.3b)
breadboards: 1

parts:
  Parte1 = Arduino Uno (Rev3)  # not connected
  Parte2 = Arduino WiFly Shield
  R1 = Resistor [tolerance=±5% resistance=10k package=THT]
  S1 = Pushbutton [package="[THT]"]

nets:
  N1: Parte2.5V, S1.Pin_1, S1.Pin_2
  N2: Parte2.D3, Parte2.GND, R1.Pin_0
  N3: R1.Pin_1, S1.Pin_3, S1.Pin_4

// code stored in the sketch: Control_remoto_led_con_WiFly.ino
#include <SPI.h>
#include "WiFly.h"
#include "Credentials.h"
 
int ledPin = 9;
 
WiFlyServer server(80);
 
void setup() {
 WiFly.begin();
 
 if (!WiFly.join(ssid, passphrase)) {
   while (1) {
   // Hang on failure.
   }
 }
 
 pinMode(ledPin,OUTPUT);
 server.begin(); // begin the server
 
 Serial.begin(9600);
 Serial.println(" ** Beginning Server ** ");
 Serial.print("IP: ");
 Serial.println(WiFly.ip());
 
 server.begin();
 
 Serial.println("Ready for commands");
 digitalWrite(ledPin, HIGH);
}
 
void loop() {
 
  WiFlyClient client = server.available();
 
  //check if their is a connection
  if (client) {
     // an http request ends with a blank line
     boolean current_line_is_blank = true;
 
     while (client.connected()) {
        // Checks if connection is still available
        if (client.available()) {
            char c = client.read();
 
            if(c == '$')
            {
                Serial.print("Client says: ");
                Serial.print(c);
                // Read the character after the $
                c = client.read();
                switch(c)
                {
                    case '1':
                    digitalWrite(ledPin, LOW);
                    Serial.println("OFF");
                    break;
                    case '2':
                    digitalWrite(ledPin, HIGH);
                    Serial.println("ON");
                    break;
                }
                // Stop reading the packet if there is a comment? #
                if(c == '#')
                {
                  Serial.println(c);
                  break;
                }
            }
         }
        // give the web browser time to receive the data
        delay(10);
     }
  }
}

// code stored in the sketch: Credentials.h.ino
#ifndef __CREDENTIALS_H__
#define __CREDENTIALS_H__

// Wifi parameters
char passphrase[] = "Tu_password";
char ssid[] = "Tu_red;

#endif

// code stored in the sketch: WiFly_WebClient_Pushigbox_modificada2.ino
// Conexión WiFly con PushingBox
// Ver.04/12/2013 a 19:50



#include <SPI.h>
#include <WiFly.h>

#include "Credentials.h"

char DEVID1[] = "mi_DevID_aqui"; //Scenario : "Activación WiFly"

uint8_t pinDevid1 = 3; //Número de Pin donde conectaremos el pulsador

boolean DEBUG = true;  // Modo Debug

char server[] = "api.pushingbox.com";  // Nombre del servidor a conectarse
boolean pinDevid1State = false; // Guarda el último estado del Pin para DevID1
boolean lastConnected = false;  // Guarda el último estado de la conexión

WiFlyClient client("api.pushingbox.com", 80);  // Indicamos Servidor y puerto de conexión

void setup() {

  Serial.begin(9600);  //Inicializamos la conexión serie
  pinMode(pinDevid1, INPUT);  // Declaramos el Pin como entrada

  WiFly.begin();  //Inicializamos la conexión Wifi

  // Si no accedemos a la red lo sigue intentando hasta conseguirlo.
  if (!WiFly.join(ssid, passphrase)) {
    Serial.println("Association failed.");
    while (1) {
      // Hang on failure.
    }
  }  
  Serial.println("connecting...1");  //Hemos conectado con la red e intentamos conectar con el servidor de PushingBox

  // Intenta conectar con el servidor de PushingBox hasta que lo consigue
  if (!client.connect()) {
    Serial.println ("connection failed");
    while (true);
  }
  else {
    Serial.println("connected 1");
  } 
}  


void loop() {


  // Escuchando el estado de pinDevid1 

  if (digitalRead(pinDevid1) == HIGH && pinDevid1State == false){ // Se ha accionado el pulsador. pinDevid1 está ON
    if(DEBUG){
      Serial.println("pinDevid1 is HIGH");
    }
    pinDevid1State = true;

    sendToPushingBox(DEVID1);  //Enviamos requerimiento a PushingBox cuando el  pinDevid1 es HIGH
  }

  if (digitalRead(pinDevid1) == LOW && pinDevid1State == true){ // Se ha dejado de accionar el pulsador. pinDevid1 está OFF
    if(DEBUG){
      Serial.println("pinDevid1 is LOW");
    }
    pinDevid1State = false;
  }

  //DEBUG part
  // Esto escribe la respuesta desde el Servidor de PushinBox
  // Deberíamos ver un  "200 OK"
  if (client.available()) {  //Escribimos lo que nos envía el Servidor
    char c = client.read();
    if(DEBUG){
      Serial.print(c);
    }
  }
  // Si no hay conexión de red, pero había la última vez a través de loop,
  // entonces detenemos la conexión
  if (!client.connected() && lastConnected) {
    if(DEBUG){
      Serial.println();
    }
    if(DEBUG){
      Serial.println("disconnecting.");
    }
    client.stop();
  }
  lastConnected = client.connected();
}

//Funcion para enviar el requerimiento a PushingBox
void sendToPushingBox(char devid[]){
  client.stop(); 
  if(DEBUG){
    Serial.println("connecting...2");
  }
  if(client.connect()){
    if(DEBUG){
      Serial.println("connected 2");
    }
    if(DEBUG){
      Serial.println("sendind request");
    }
    client.print("GET /pushingbox?devid=");
    client.print(devid);
    client.println(" HTTP/1.1");
    client.print("Host: ");
    client.println(server);
    client.println("User-Agent: Arduino");
    client.println();
  }
  else {
    if(DEBUG){
      Serial.println("connection failed");
    }
  }
}
